# Fritzing sketch Aquaduino Sketch (saved by Fritzing 0.9.2b)
breadboards: 1

parts:
  Pro_Micro1 = Pro Micro
  T1 = LM35 Temperature Sensor [package="TO92 [THT]"]
  MIC1 = Microphone
  Q1 = Basic FET P-Channel [package="TO220 [THT]"]
  Q2 = Basic FET P-Channel [package="TO220 [THT]"]
  Q3 = Basic FET P-Channel [package="TO220 [THT]"]
  Q4 = Basic FET P-Channel [package="TO220 [THT]"]
  BAT1 = Battery Holders [package=battcon_12mm]
  OLED1 = 128x32 I2C Monochrome OLED Display
  IC2 = DS1307 [package=THT]
  BUTTON1 = Arcade Button (red)
  S1 = Toggle Switch [package=THT]
  IC3 = L293D [package=THT]  # not connected
  LED1 = RGB LED - (4 legs) [package="5 mm [THT]"]
  R1 = Resistor [tolerance=±5% resistance=220 package=THT]
  Y1 = CRYSTAL [package=tc26h]  # not connected

nets:
  GND: Pro_Micro1.GND, T1.GND, MIC1.pin1, Q1.source, Q2.source, Q3.source, Q4.source, BAT1.-, OLED1.GND, IC2.0V, BUTTON1.no_name_yet#1, S1.L1
  N1: Pro_Micro1.D2, OLED1.SDA
  N2: Pro_Micro1.D3, OLED1.SCL
  N3: Pro_Micro1.D4, MIC1.pin2
  N4: Pro_Micro1.D6, BUTTON1.no_name_yet#2
  N5: Pro_Micro1.D7, T1.Vout
  N6: Pro_Micro1.D10, Q1.drain
  N7: Pro_Micro1.D16/MOSI, Q2.drain
  N8: Pro_Micro1.D14/MISO, Q3.drain
  N9: Pro_Micro1.D15/SCLK, Q4.drain
  VCC: Pro_Micro1.VCC, T1.+Vs, Q1.gate, Q2.gate, Q3.gate, Q4.gate, OLED1.3.3V, LED1.red_cathode, R1.Pin_1

custom parts:
  Pro Micro: The SparkFun Pro Micro is a complete USB-based microcontoller development system, in a very small footprint, capable of implementing many types of projects. All programming can be done via the USB port.
  Arcade Button (red): Adafruit Arcade Button (red)
